# Fritzing sketch ledcube (saved by Fritzing 0.9.3b)

parts:
  U1 = 74HC595 [package="DIP16 [THT]"]
  Part1 = Arduino Nano (Rev3.0)
  U6 = 74HC595 [package="DIP16 [THT]"]
  U7 = 74HC595 [package="DIP16 [THT]"]
  U8 = 74HC595 [package="DIP16 [THT]"]
  U9 = 74HC595 [package="DIP16 [THT]"]
  U10 = 74HC595 [package="DIP16 [THT]"]
  U11 = 74HC595 [package="DIP16 [THT]"]
  R9 = Resistor [tolerance=±10% resistance=75 package=THT]
  R10 = Resistor [tolerance=±10% resistance=75 package=THT]
  R11 = Resistor [tolerance=±10% resistance=75 package=THT]
  R12 = Resistor [tolerance=±10% resistance=75 package=THT]
  R13 = Resistor [tolerance=±10% resistance=75 package=THT]
  R14 = Resistor [tolerance=±10% resistance=75 package=THT]
  LED1 = LED - 3mm [color="Orange (620nm)" package="3 mm [THT]"]
  LED2 = LED - 3mm [color="Orange (620nm)" package="3 mm [THT]"]
  LED3 = LED - 3mm [color="Orange (620nm)" package="3 mm [THT]"]
  LED4 = LED - 3mm [color="Orange (620nm)" package="3 mm [THT]"]
  LED5 = LED - 3mm [color="Orange (620nm)" package="3 mm [THT]"]
  LED6 = LED - 3mm [color="Orange (620nm)" package="3 mm [THT]"]

nets:
  N1: U1.Q1, R10.Pin_1
  N2: U1.Q2, R9.Pin_1
  N3: U1.Q3, R12.Pin_1
  N4: U1.Q4, R11.Pin_1
  N5: U1.Q5, R14.Pin_1
  N6: U1.Q6, R13.Pin_1
  GND: U1.GND, U1.OE, Part1.GND, U6.OE, U7.OE, U8.OE, U9.OE, U10.OE, U11.OE
  VCC: U1.MR, U1.VCC, Part1.5V, U6.MR, U7.MR, U8.MR, U9.MR, U10.MR, U11.MR
  N7: U1.SH_CP, Part1.D6, U6.SH_CP, U7.SH_CP, U8.SH_CP, U9.SH_CP, U10.SH_CP, U11.SH_CP
  N8: U1.ST_CP, Part1.D5, U6.ST_CP, U7.ST_CP, U8.ST_CP, U9.ST_CP, U10.ST_CP, U11.ST_CP
  N9: U1.DS, U7.Q7'
  N10: Part1.D4, U11.DS
  GND_2: U6.GND, U7.GND, U8.GND, U9.GND, U10.GND, U11.GND
  N11: U6.Q7', U7.DS
  N12: U6.DS, U8.Q7'
  VCC_2: U6.VCC, U7.VCC, U8.VCC, U9.VCC, U10.VCC, U11.VCC
  N13: U8.DS, U9.Q7'
  N14: U9.DS, U10.Q7'
  N15: U10.DS, U11.Q7'
  N16: U11.Q1, LED1.anode
  N17: U11.Q2, LED2.anode
  N18: U11.Q3, LED3.anode
  N19: U11.Q4, LED4.anode
  N20: U11.Q5, LED5.anode
  N21: U11.Q6, LED6.anode
  N22: R10.Pin_0, LED1.cathode, LED2.cathode, LED3.cathode, LED4.cathode, LED5.cathode, LED6.cathode

notes:
  These shift registers each control one row (36 leds)
  The wires from the shift registers connect to the bottom led of each row
  Same is repeated for the other 5 shift registers
  This shift register controls each of the 6 levels ↑
